# Fritzing sketch senseoNano (saved by Fritzing 0.9.3b)
circuit board: 24.6373cm x 10.8477cm
breadboards: 1

parts:
  Part1 = Arduino Nano (Rev3.0)
  J1 = female pin header, 2 pins [form="♀ (female)"]
  4n35_read_LED = Optocoupler [package=THT]
  R2 = Resistor [tolerance=±5% resistance=330 package=THT]
  R1 = Resistor [tolerance=±1% resistance=3.09k package=THT]
  R3 = Resistor [tolerance=±5% resistance=27k package=THT]
  J3 = screw terminal, 3 pins
  4n35_read_LED1 = Optocoupler [package=THT]
  4n35_read_LED2 = Optocoupler [package=THT]
  4n35_read_LED3 = Optocoupler [package=THT]
  4n35_read_LED4 = Optocoupler [package=THT]
  4n35_read_LED5 = Optocoupler [package=THT]
  4n35_read_LED6 = Optocoupler [package=THT]
  J4 = screw terminal, 3 pins
  J5 = screw terminal, 3 pins
  J6 = screw terminal, 3 pins
  J7 = screw terminal, 3 pins
  J8 = screw terminal, 3 pins
  J9 = screw terminal, 3 pins
  R4 = Resistor [tolerance=±1% resistance=3.09k package=THT]
  R5 = Resistor [tolerance=±1% resistance=3.09k package=THT]
  R6 = Resistor [tolerance=±1% resistance=3.09k package=THT]
  R7 = Resistor [tolerance=±5% resistance=27k package=THT]
  R8 = Resistor [tolerance=±5% resistance=27k package=THT]
  R9 = Resistor [tolerance=±5% resistance=27k package=THT]
  R10 = Resistor [tolerance=±5% resistance=330 package=THT]
  R11 = Resistor [tolerance=±5% resistance=330 package=THT]
  R12 = Resistor [tolerance=±5% resistance=330 package=THT]
  R13 = Resistor [tolerance=±5% resistance=320 package=THT]
  R14 = Resistor [tolerance=±5% resistance=320 package=THT]
  R15 = Resistor [tolerance=±5% resistance=320 package=THT]

nets:
  N1: Part1.GND, J1.pin2, R3.Pin_1, R7.Pin_1, R8.Pin_1, R9.Pin_1, R13.Pin_0, R14.Pin_0, R15.Pin_0
  N2: Part1.D2, 4n35_read_LED.Pin_4, R3.Pin_0
  N3: Part1.D4, 4n35_read_LED2.Pin_1
  N4: Part1.D5, 4n35_read_LED1.Pin_4, R7.Pin_0
  N5: Part1.D6, 4n35_read_LED3.Pin_1
  N6: Part1.D7, 4n35_read_LED4.Pin_4, R8.Pin_0
  N7: Part1.D8, 4n35_read_LED5.Pin_1
  N8: Part1.D11/MOSI, 4n35_read_LED6.Pin_4, R9.Pin_0
  N9: Part1.5V, J1.pin1, R1.Pin_1, R4.Pin_1, R5.Pin_1, R6.Pin_1
  N10: 4n35_read_LED.Pin_1, R2.Pin_0, J3.pin2
  N11: 4n35_read_LED.Pin_2, J3.pin1
  N12: 4n35_read_LED.Pin_5, R1.Pin_0
  N13: R2.Pin_1, J3.pin3
  N14: 4n35_read_LED1.Pin_1, J5.pin2, R10.Pin_0
  N15: 4n35_read_LED1.Pin_2, J5.pin1
  N16: 4n35_read_LED1.Pin_5, R4.Pin_0
  N17: 4n35_read_LED2.Pin_2, R15.Pin_1
  N18: 4n35_read_LED2.Pin_4, J4.pin1
  N19: 4n35_read_LED2.Pin_5, J4.pin3
  N20: 4n35_read_LED2.Pin_6, J4.pin2
  N21: 4n35_read_LED3.Pin_2, R14.Pin_1
  N22: 4n35_read_LED3.Pin_4, J6.pin1
  N23: 4n35_read_LED3.Pin_5, J6.pin3
  N24: 4n35_read_LED3.Pin_6, J6.pin2
  N25: 4n35_read_LED4.Pin_1, J7.pin2, R11.Pin_0
  N26: 4n35_read_LED4.Pin_2, J7.pin1
  N27: 4n35_read_LED4.Pin_5, R5.Pin_0
  N28: 4n35_read_LED5.Pin_2, R13.Pin_1
  N29: 4n35_read_LED5.Pin_4, J8.pin1
  N30: 4n35_read_LED5.Pin_5, J8.pin3
  N31: 4n35_read_LED5.Pin_6, J8.pin2
  N32: 4n35_read_LED6.Pin_1, J9.pin2, R12.Pin_0
  N33: 4n35_read_LED6.Pin_2, J9.pin1
  N34: 4n35_read_LED6.Pin_5, R6.Pin_0
  N35: J5.pin3, R10.Pin_1
  N36: J7.pin3, R11.Pin_1
  N37: J9.pin3, R12.Pin_1

notes:
  statusLEDplus
  statusLEDminus
  smallButtonRead
  powerButtonRead
  largeButtonRead
  LED Out GRB
  PadSensor
  LidSensor
  RX+TX
  CupSensor
